# Fritzing sketch Schema (saved by Fritzing 0.9.3b)
breadboards: 2

parts:
  Part1 = Arduino Uno (Rev3)
  LCD1 = LCD screen
  U1 = POT [package=pot_alpha_rv16af-20]

nets:
  GND: Part1.D11_PWM/MOSI, Part1.GND, LCD1.VSS, LCD1.R/W, LCD1.LED-, U1.A
  N1: Part1.D12/MISO, LCD1.RS
  N2: Part1.D2, LCD1.DB7
  N3: Part1.D3_PWM, LCD1.DB6
  N4: Part1.D4, LCD1.DB5
  N5: Part1.D5_PWM, LCD1.DB4
  5V: Part1.5V, LCD1.VDD, LCD1.LED+, U1.E
  N6: LCD1.V0, U1.S
